# Fritzing sketch Assignment 2 (saved by Fritzing 0.9.10b)

parts:
  M5Stack-ATOM-Matrix1 = atom-matrix [package=M5Stack]
  S1 = Pushbutton [package=THT]

nets:
  N1: M5Stack-ATOM-Matrix1.G32, S1.leg1
  N2: M5Stack-ATOM-Matrix1.GNDb, S1.leg0

custom parts:
  atom-matrix: M5Stack ATOM Matrix
