# Fritzing sketch adv Prototyping - Project 1 -Michael Tu (saved by Fritzing 0.9.10b)
breadboards: 1

parts:
  M5Stack-ATOM-Matrix1 = atom-matrix [package=M5Stack]
  LED1 = smd LED [color="Yellow (595nm)" package="0603 [SMD]"]
  R1 = Resistor [tolerance=±5% power=0.25 resistance=150 package=THT]
  R2 = Resistor [tolerance=±5% power=0.25 resistance=150 package=THT]
  LED2 = smd LED [color="Yellow (595nm)" package="0603 [SMD]"]
  S1 = Pushbutton [package=THT]

nets:
  N1: M5Stack-ATOM-Matrix1.G26, S1.leg0
  N2: M5Stack-ATOM-Matrix1.5Vb, R1.Pin_1, R2.Pin_1
  N3: M5Stack-ATOM-Matrix1.GNDb, LED1.cathode, LED2.cathode, S1.leg1
  N4: LED1.anode, R1.Pin_0
  N5: R2.Pin_0, LED2.anode

custom parts:
  atom-matrix: M5Stack ATOM Matrix
